# Fritzing sketch Blink (saved by Fritzing 0.9.3b)
breadboards: 1

parts:
  Part1 = Arduino Uno (Rev3) - ICSP
  R1 = Resistor [tolerance=±5% resistance=330 package=THT]
  S1 = Momentary Switch [package=ksa_sealed_tac_switch]
  R2 = Resistor [tolerance=±5% resistance=330 package=THT]
  LED2 = LEDs [package=led10mm]
  LED1 = LEDs [package=led10mm]

nets:
  N1: Part1.5V, S1.1
  N2: Part1.D9_PWM, R1.Pin_0
  GND: Part1.GND, LED2.C, LED1.C
  N3: R1.Pin_1, LED1.A
  N4: S1.3, R2.Pin_1
  N5: R2.Pin_0, LED2.A
